// Digital circuit 4bit-Ripple‑Carry .dig as structural Verilog
module _4bit_Ripple_Carry (
  input  [3:0] A,
  input  [3:0] B,
  input  carry_in,
  output [3:0] Sum,
  output out_5
);

  wire hw1_bit_full_adder_2_carry_out, hw1_bit_full_adder_3_carry_out, hw1_bit_full_adder_4_carry_out;

  Hw1_bit_Full_Adder hw1_bit_full_adder_1 (
    .a(A[3]), .b(B[3]), .carry_in(hw1_bit_full_adder_2_carry_out), .sum(Sum[3]), .carry_out(out_5));
  Hw1_bit_Full_Adder hw1_bit_full_adder_2 (
    .a(A[2]), .b(B[2]), .carry_in(hw1_bit_full_adder_3_carry_out), .sum(Sum[2]),
    .carry_out(hw1_bit_full_adder_2_carry_out));
  Hw1_bit_Full_Adder hw1_bit_full_adder_3 (
    .a(A[1]), .b(B[1]), .carry_in(hw1_bit_full_adder_4_carry_out), .sum(Sum[1]),
    .carry_out(hw1_bit_full_adder_3_carry_out));
  Hw1_bit_Full_Adder hw1_bit_full_adder_4 (
    .a(A[0]), .b(B[0]), .carry_in(carry_in), .sum(Sum[0]), .carry_out(hw1_bit_full_adder_4_carry_out));
endmodule
